# Fritzing sketch PCBfile (saved by Fritzing 0.9.3b)
circuit board: 6.24228cm x 5.2145cm
breadboards: 1

parts:
  J2 = female pin header, 4 pins [form="♀ (female)"]
  J3 = female pin header, 4 pins [form="♀ (female)"]
  R2 = Resistor [tolerance=±5% resistance=2.2k package=THT]
  J4 = shrouded pin header, 20 pins [form="♂ (shrouded male)"]
  R1 = Resistor [tolerance=±5% resistance=1k package=THT]

nets:
  N1: J2.pin1, J3.pin1, R2.Pin_0, J4.pin11
  N2: J2.pin2, R1.Pin_1
  N3: J2.pin3, J4.pin13
  N4: J2.pin4, J3.pin2, J4.pin20
  N5: J3.pin3, J4.pin2
  N6: J3.pin4, J4.pin3
  N7: R2.Pin_1, J4.pin12, R1.Pin_0

notes:
  Saina Kapoor
  VCC
  SDA
  SCL
  TRIG
  RES.
  GND
  R2
  ECHO
  R1
  HC-SR04
  LCD
