# Fritzing sketch ceng317 (saved by Fritzing 0.9.3b)
circuit board: 8.67363cm x 5.79496cm
breadboards: 1

parts:
  hc-sr1 = hc-sr04
  Raspberry_Pi_1 = Raspberry Pi 3 [part_number=RPI-3-V1.2]
  Part1 = LCD1602-I2C
  R4 = Resistor [tolerance=±5% resistance=1k package=THT]
  R3 = Resistor [tolerance=±5% resistance=2k package=THT]

nets:
  VCC: hc-sr1.VCC, Raspberry_Pi_1.5V, Part1.VCC
  N1: hc-sr1.Trig, Raspberry_Pi_1.GIPO23
  N2: hc-sr1.Echo, R4.Pin_1
  GND: hc-sr1.GND, Raspberry_Pi_1.GND, Part1.GND, R3.Pin_0
  N3: Raspberry_Pi_1.GPIO2, Part1.SDA
  N4: Raspberry_Pi_1.GPIO3, Part1.SCL
  N5: Raspberry_Pi_1.GIPO24, R4.Pin_0, R3.Pin_1

custom parts:
  LCD1602-I2C: A standard character display, usually with 2x16 characters. Comes in many colors with LCM1602 IIC attached.
