# Fritzing sketch ceng317R (saved by Fritzing 0.9.3b)
circuit board: 8.46667cm x 5.64444cm
breadboards: 1

parts:
  J2 = shrouded pin header, 20 pins [form="♂ (shrouded male)"]
  J3 = female pin header, 4 pins [form="♀ (female)"]
  J4 = female pin header, 4 pins [form="♀ (female)"]
  R2 = Resistor [tolerance=±5% resistance=2k package=THT]
  R1 = Resistor [tolerance=±5% resistance=1k package=THT]

nets:
  N1: J2.pin2, J4.pin3
  N2: J2.pin3, J4.pin4
  N3: J2.pin11, J3.pin4, J4.pin1, R2.Pin_0
  N4: J2.pin12, R2.Pin_1, R1.Pin_0
  N5: J2.pin13, J3.pin2
  N6: J2.pin20, J3.pin1, J4.pin2
  N7: J3.pin3, R1.Pin_1

notes:
  Saina Kapoor
  GND
  VCC
  SDA
  SCL
  TRIG
  ECHO
  R2
  R1
  R
  RPI
  HC-SR04
  LCD
